# Fritzing sketch Schaltplan AUTOSAR (saved by Fritzing 0.9.3b)
breadboards: 2

parts:
  U1 = PCF8574 [package="DIP16 [THT]"]
  LED1 = LED - 5mm [color="Yellow (595nm)" package="5 mm [THT]"]
  LED2 = LED - 5mm [color="Yellow (595nm)" package="5 mm [THT]"]
  LED3 = LED - 5mm [color="Yellow (595nm)" package="5 mm [THT]"]
  LED4 = LED - 5mm [color="Yellow (592nm)" package="5 mm [THT]"]
  R1 = Resistor [tolerance=±5% resistance=1k package=THT]
  R2 = Resistor [tolerance=±5% resistance=1k package=THT]
  R4 = Resistor [tolerance=±5% resistance=1k package=THT]
  R3 = Resistor [tolerance=±5% resistance=1k package=THT]
  R5 = Resistor [tolerance=±5% resistance=82k package=THT]
  C1 = Tantalum Capacitor [capacitance=1μF package="100 mil [THT, tantalum]"]
  R6 = Resistor [tolerance=±5% resistance=82k package=THT]

nets:
  N1: U1.A0, U1.A1, U1.A3, U1.GND
  N2: U1.P0, R4.Pin_0
  N3: U1.P1, R3.Pin_1
  N4: U1.P2, R2.Pin_0
  N5: U1.P3, R1.Pin_1
  N6: U1.SCL, R6.Pin_0
  N7: U1.SDA, R5.Pin_0
  N8: LED1.cathode, R1.Pin_0
  N9: LED1.anode, LED2.anode, LED3.anode, LED4.anode, R5.Pin_1, C1.-, R6.Pin_1
  N10: LED2.cathode, R3.Pin_0
  N11: LED3.cathode, R2.Pin_1
  N12: LED4.cathode, R4.Pin_1

notes:
  - GRND
  - GRND
  - VBUS
  - SCL
  - SDA
